# Fritzing sketch sensor-circuit (saved by Fritzing 0.9.2b)
breadboards: 1

parts:
  Part1 = Arduino Micro (Rev3)  # not connected
  DHT1 = DHT22 Humidity and Temperature Sensor
  R1 = Resistor [tolerance=±0.25% resistance=1k package=THT]
  Part2 = FC-28 Soil Hygrometer Module - Probe  # not connected
  Part3 = FC-28 Soil Hygrometer Module

nets:
  VDD: DHT1.VDD, R1.Pin_0, Part3.VCC
  N1: DHT1.DATA, R1.Pin_1
  GND: DHT1.GND, Part3.GND

custom parts:
  FC-28 Soil Hygrometer Module - Probe: The FC-28 is a soil hygrometer module that uses the Texas Instruments LM393 comparator chip to provide an analog measurement of soil humidity.
  FC-28 Soil Hygrometer Module: The FC-28 is a soil hygrometer module that uses the Texas Instruments LM393 comparator chip to provide an analog measurement of soil humidity. The digital output is high when soil moisture is over a certain threshold, as determined by adjusting the potentiometer.
